# Fritzing sketch Untitled Sketch (saved by Fritzing 0.9.3b)
breadboards: 2

parts:
  U4 = MAX6675 [package=so08]
  Componente1 = Gas Sensor Breakout Board
  PIR1 = PIR sensor
  PIR2 = PIR sensor
  J1 = Piezo Speaker
  Componente2 = Logic Level Converter
  U1 = ESP32-38PinWide [part_number=ESP32-38PinWide]
  U7 = RELAY [package=relay-jzc]

nets:
  VDD: U4.VDD, Componente1.H1, PIR1.VDD, PIR2.VDD, U1.3.3
  N1: U4.SCK, U1.GPIO32
  N2: U4.CS, U1.GPIO33
  N3: U4.MISO, U1.GPIO25
  N4: Componente1.A1, U1.GPIO35
  GND: Componente1.GND, PIR1.GND, PIR2.GND, Componente2.GND, U1.GND
  N5: PIR1.SIG, Componente2.RX2_HV
  N6: PIR2.SIG, Componente2.TX2_HV
  N7: J1.pin2, Componente2.TX_LV
  N8: Componente2.TX2_LV, U1.GPIO4
  N9: Componente2.RX2_LV, U1.GPIO13
  N10: Componente2.TX_HV, U1.GPIO21
  N11: Componente2.HV, U1.VIN
  N12: U1.GPIO15, U7.MAIN

notes:
  1Gnd 4Vdd 7So
  2T- 6Cs
  3T+ 5CLK
  Válvula Solenóide

custom parts:
  ESP32-38PinWide: Generic 38-Pin ESP32 with wide format (only access to one side of pins on a breadboard) based on Stephen Lilley's HiLetgo ESP-WROOM-32 ESP32 ESP-32S Development Board.
